# Fritzing sketch deepsleep_connection (saved by Fritzing 0.9.3b)
circuit board: 8.46667cm x 5.64444cm
breadboards: 1

parts:
  MC = Arduino Nano (Rev3.0)
  U1 = DS1307 [package=so08]
  C1 = Electrolytic Capacitor [package="100 mil [THT, electrolytic]"]

nets:
  GND: MC.GND, U1.GND
  5V: MC.VIN, U1.VCC
  N1: MC.RESET, C1.-
  N2: MC.A5, U1.SCL
  N3: MC.A4, U1.SDA
  N4: U1.SQW, C1.+

custom parts:
  Electrolytic Capacitor: A small electrolytic capacitor
